# Fritzing sketch gps (saved by Fritzing 0.9.3b)
circuit board: 19.0264cm x 13.4812cm
breadboards: 1

parts:
  GPS = GP-2106 [package=gp-2106]
  microSD = SparkFun - microSD Transflash
  Часть2 = Arduino Uno (Rev3)
  VCC1 = Battery  # not connected
  Часть3 = Bluetooth HC-05 Macho
  S2 = Momentary Switch [package=ksa_sealed_tac_switch]
  S3 = Momentary Switch [package=ksa_sealed_tac_switch]
  S4 = Momentary Switch [package=ksa_sealed_tac_switch]  # not connected
  LCM1602_IIC1 = LCM1602 IIC [part_number="LCM1602 IIC" chip_label="LCM1602 IIC" package="DIP (Dual Inline) [THT]"]
  LCD1 = LCD screen

nets:
  GND: GPS.GND, Часть2.GND, Часть3.GND, LCM1602_IIC1.GND
  N1: GPS.RX, Часть2.D3_PWM
  N2: GPS.TX, Часть2.D5_PWM
  VCC: GPS.VCC, Часть2.3V3
  N3: microSD.CS, Часть2.D4
  N4: Часть2.A4/SDA, LCM1602_IIC1.SDA
  N5: Часть2.A5/SCL, LCM1602_IIC1.SCL
  N6: Часть2.D0/RX, S3.4
  N7: Часть2.D1/TX, Часть3.RXD
  5V: Часть2.5V, S2.2, LCM1602_IIC1.VCC
  N8: Часть3.TXD, S3.3
  N9: Часть3.VCC, S2.4
  VSS: LCM1602_IIC1.VSS, LCD1.VSS
  VDD: LCM1602_IIC1.VDD, LCD1.VDD
  N10: LCM1602_IIC1.V0, LCD1.V0
  N11: LCM1602_IIC1.RS, LCD1.RS
  N12: LCM1602_IIC1.RW, LCD1.R/W
  N13: LCM1602_IIC1.E, LCD1.E
  N14: LCM1602_IIC1.D0, LCD1.DB0
  N15: LCM1602_IIC1.D1, LCD1.DB1
  N16: LCM1602_IIC1.D2, LCD1.DB2
  N17: LCM1602_IIC1.D3, LCD1.DB3
  N18: LCM1602_IIC1.D4, LCD1.DB4
  N19: LCM1602_IIC1.D5, LCD1.DB5
  N20: LCM1602_IIC1.D6, LCD1.DB6
  N21: LCM1602_IIC1.D7, LCD1.DB7
  N22: LCM1602_IIC1.A, LCD1.LED+
  N23: LCM1602_IIC1.K, LCD1.LED-

notes:
  DO - MOSI
  CD - MISO

custom parts:
  LCM1602 IIC: I2C-Module to use a 1602 or 2004 LCD on with the wire.h libory Serial LCD Modul
